// Logisim project hw_vga_sim.circ as structural Verilog: 1 circuit, main circuit main
module main (
  input  nRST
);

  wire CLK_out, comparator_2_eq, n7411_1_pin1, n7411_1_pin2, n7411_1_pin4, n7411_1_pin5, n7411_1_pin6,
       n74163_1_pin1, n74163_1_pin3, n74163_1_pin7, n74163_1_pin15, n74163_2_pin3, n74163_2_pin7,
       n74163_2_pin9, n74163_2_pin10, n74163_2_pin15, n74163_3_pin15, n74163_4_pin15;
  wire [0:0] n7411_1_pin8, n7411_2_pin8;
  wire [3:0] n74163_2_pin14, n74163_4_pin14, n74163_6_pin15;
  wire [11:0] n74163_1_pin14;

  Clock CLK (.out(CLK_out));
  _74163 #(.ShowInternalStructure("true")) u_74163_1 (
    .pin1(n74163_1_pin1), .pin2(CLK_out), .pin3(n74163_1_pin3), .pin4(n74163_1_pin3), .pin5(n74163_1_pin3),
    .pin6(n74163_1_pin3), .pin7(n74163_1_pin7), .pin15(n74163_1_pin15), .pin14(n74163_1_pin14[0]),
    .pin13(n74163_1_pin14[1]), .pin12(n74163_1_pin14[2]), .pin11(n74163_1_pin14[3]), .pin10(n74163_1_pin7),
    .pin9(n74163_1_pin7));
  _7411 #(.ShowInternalStructure("true")) u_7411_1 (
    .pin1(n7411_1_pin1), .pin2(n7411_1_pin2), .pin3(nRST), .pin4(n7411_1_pin4), .pin5(n7411_1_pin5),
    .pin6(n7411_1_pin6), .pin13(nRST), .pin12(n74163_1_pin1), .pin11(n74163_1_pin14[0]),
    .pin10(n74163_1_pin14[1]), .pin9(n74163_1_pin14[2]), .pin8(n7411_1_pin8[0]));
  _74163 #(.ShowInternalStructure("true")) u_74163_2 (
    .pin1(n7411_1_pin6), .pin2(CLK_out), .pin3(n74163_2_pin3), .pin4(n74163_2_pin3), .pin5(n74163_2_pin3),
    .pin6(n74163_2_pin3), .pin7(n74163_2_pin7), .pin15(n74163_2_pin15), .pin14(n74163_2_pin14[0]),
    .pin13(n74163_2_pin14[1]), .pin12(n74163_2_pin14[2]), .pin11(n74163_2_pin14[3]), .pin10(n74163_2_pin10),
    .pin9(n74163_2_pin9));
  _74163 #(.ShowInternalStructure("true")) u_74163_3 (
    .pin1(n74163_1_pin1), .pin2(CLK_out), .pin3(n74163_1_pin3), .pin4(n74163_1_pin3), .pin5(n74163_1_pin3),
    .pin6(n74163_1_pin3), .pin7(n74163_1_pin15), .pin15(n74163_3_pin15), .pin14(n74163_1_pin14[4]),
    .pin13(n74163_1_pin14[5]), .pin12(n74163_1_pin14[6]), .pin11(n74163_1_pin14[7]), .pin10(n74163_1_pin15),
    .pin9(n74163_1_pin7));
  _74163 #(.ShowInternalStructure("true")) u_74163_4 (
    .pin1(n7411_1_pin6), .pin2(CLK_out), .pin3(n74163_2_pin3), .pin4(n74163_2_pin3), .pin5(n74163_2_pin3),
    .pin6(n74163_2_pin3), .pin7(n74163_2_pin15), .pin15(n74163_4_pin15), .pin14(n74163_4_pin14[0]),
    .pin13(n74163_4_pin14[1]), .pin12(n74163_4_pin14[2]), .pin11(n74163_4_pin14[3]), .pin10(n74163_2_pin15),
    .pin9(n74163_2_pin9));
  Hex_Digit_Display hex_digit_display_1 (.value(n74163_6_pin15));  // open: dp
  _7411 #(.ShowInternalStructure("true")) u_7411_2 (
    .pin11(n74163_2_pin14[2]), .pin10(n74163_2_pin14[3]), .pin9(n74163_6_pin15[1]), .pin8(n7411_2_pin8[0]));  // open: pin1, pin2, pin3, pin4, pin5, pin6, pin13, pin12
  Hex_Digit_Display hex_digit_display_2 (.value(n74163_1_pin14[11:8]));  // open: dp
  Hex_Digit_Display hex_digit_display_3 (.value(n74163_1_pin14[7:4]));  // open: dp
  Hex_Digit_Display hex_digit_display_4 (.value(n74163_4_pin14));  // open: dp
  Hex_Digit_Display hex_digit_display_5 (.value(n74163_2_pin14));  // open: dp
  Hex_Digit_Display hex_digit_display_6 (.value(n74163_1_pin14[3:0]));  // open: dp
  _74163 #(.ShowInternalStructure("true")) u_74163_5 (
    .pin1(n74163_1_pin1), .pin2(CLK_out), .pin3(n74163_1_pin3), .pin4(n74163_1_pin3), .pin5(n74163_1_pin3),
    .pin6(n74163_1_pin3), .pin7(n74163_3_pin15), .pin14(n74163_1_pin14[8]), .pin13(n74163_1_pin14[9]),
    .pin12(n74163_1_pin14[10]), .pin11(n74163_1_pin14[11]), .pin10(n74163_3_pin15), .pin9(n74163_1_pin7));  // open: pin15
  _74163 #(.ShowInternalStructure("true")) u_74163_6 (
    .pin1(n7411_1_pin6), .pin2(CLK_out), .pin3(n74163_2_pin3), .pin4(n74163_2_pin3), .pin5(n74163_2_pin3),
    .pin6(n74163_2_pin3), .pin7(n74163_4_pin15), .pin15(n74163_6_pin15[0]), .pin14(n74163_6_pin15[1]),
    .pin13(n74163_6_pin15[2]), .pin12(n74163_6_pin15[3]), .pin10(n74163_4_pin15), .pin9(n74163_2_pin9));  // open: pin11
  not not_1 (n7411_1_pin2, n74163_2_pin10);
  Comparator #(.mode("unsigned")) comparator_1 (
    .a({n74163_1_pin14[9:3], n7411_1_pin8[0]}), .b(8'hc7), .eq(n74163_2_pin10));  // open: gt, lt
  Comparator #(.mode("unsigned")) comparator_2 (
    .a({n74163_6_pin15[0], n74163_4_pin14, n74163_2_pin14[1:0], n7411_2_pin8[0]}), .b(8'h1),
    .eq(comparator_2_eq));  // open: gt, lt
  not not_2 (n7411_1_pin5, comparator_2_eq);
  // also tied to GND on the sheet: {n74163_1_pin3, n74163_2_pin3}
  // also tied to VCC on the sheet: {n74163_1_pin7, n7411_1_pin1, n74163_2_pin9, n7411_1_pin4, n74163_2_pin7}
endmodule
